// Logisim project TERM2FINAL.circ as structural Verilog: 6 circuits, main circuit senso_fianl
module main_system (
  input  LS4,
  input  LS3,
  input  LS2,
  input  LS1,
  input  Reset
);

  wire Number_of_people_Counting_System_out_19, Number_of_people_Counting_System_out_20,
       Number_of_people_Counting_System_out_21, Number_of_people_Counting_System_out_22,
       Number_of_people_Counting_System_out_23, Number_of_people_Counting_System_out_24,
       Number_of_people_Counting_System_out_25, Number_of_people_Counting_System_out_26,
       Number_of_people_Counting_System_out_27, Number_of_people_Counting_System_out_28,
       Number_of_people_Counting_System_out_29, Number_of_people_Counting_System_out_30,
       Number_of_people_Counting_System_out_31, Number_of_people_Counting_System_out_32,
       Number_of_people_Counting_System_out_33, Number_of_people_Counting_System_out_34,
       Number_of_people_Counting_System_out_35, Number_of_people_Counting_System_out_36,
       Number_of_people_Counting_System_out_37, Number_of_people_Counting_System_out_38,
       Number_of_people_Counting_System_out_39, Number_of_seats_counting_system_out_19,
       Number_of_seats_counting_system_out_20, Number_of_seats_counting_system_out_21,
       Number_of_seats_counting_system_out_22, Number_of_seats_counting_system_out_23,
       Number_of_seats_counting_system_out_24, Number_of_seats_counting_system_out_25,
       Number_of_seats_counting_system_out_26, Number_of_seats_counting_system_out_27,
       Number_of_seats_counting_system_out_28, Number_of_seats_counting_system_out_29,
       Number_of_seats_counting_system_out_30, Number_of_seats_counting_system_out_31,
       Number_of_seats_counting_system_out_32, Number_of_seats_counting_system_out_33,
       Number_of_seats_counting_system_out_34, Number_of_seats_counting_system_out_35,
       Number_of_seats_counting_system_out_36, Number_of_seats_counting_system_out_37,
       Number_of_seats_counting_system_out_38, Number_of_seats_counting_system_out_39,
       senso_fianl_1_counted_enter, senso_fianl_1_counted_exit, up_counter_1_out_3, up_counter_1_out_4,
       up_counter_1_out_5, up_counter_1_out_6, up_counter_1_out_7, up_counter_1_out_8, up_counter_1_out_9,
       up_counter_1_out_10, up_counter_2_out_3, up_counter_2_out_4, up_counter_2_out_5, up_counter_2_out_6,
       up_counter_2_out_7, up_counter_2_out_8, up_counter_2_out_9, up_counter_2_out_10, up_counter_3_out_3,
       up_counter_3_out_4, up_counter_3_out_5, up_counter_3_out_6, up_counter_3_out_7, up_counter_3_out_8,
       up_counter_3_out_9, up_counter_3_out_10, up_counter_4_out_3, up_counter_4_out_4, up_counter_4_out_5,
       up_counter_4_out_6, up_counter_4_out_7, up_counter_4_out_8, up_counter_4_out_9, up_counter_4_out_10;

  senso_fianl senso_fianl_1 (
    .Counted_Enter(senso_fianl_1_counted_enter), .Counted_Exit(senso_fianl_1_counted_exit), .in_1(Reset),
    .LS1(LS1), .LS2(LS2), .LS3(LS3), .LS4(LS4));
  up_counter up_counter_1 (
    .CK(senso_fianl_1_counted_enter), .RS(Reset), .out_3(up_counter_1_out_3), .out_4(up_counter_1_out_4),
    .out_5(up_counter_1_out_5), .out_6(up_counter_1_out_6), .out_7(up_counter_1_out_7),
    .out_8(up_counter_1_out_8), .out_9(up_counter_1_out_9), .out_10(up_counter_1_out_10));
  up_counter up_counter_2 (
    .CK(senso_fianl_1_counted_exit), .RS(Reset), .out_3(up_counter_2_out_3), .out_4(up_counter_2_out_4),
    .out_5(up_counter_2_out_5), .out_6(up_counter_2_out_6), .out_7(up_counter_2_out_7),
    .out_8(up_counter_2_out_8), .out_9(up_counter_2_out_9), .out_10(up_counter_2_out_10));
  up_counter up_counter_3 (
    .CK(senso_fianl_1_counted_enter), .RS(Reset), .out_3(up_counter_3_out_3), .out_4(up_counter_3_out_4),
    .out_5(up_counter_3_out_5), .out_6(up_counter_3_out_6), .out_7(up_counter_3_out_7),
    .out_8(up_counter_3_out_8), .out_9(up_counter_3_out_9), .out_10(up_counter_3_out_10));
  up_counter up_counter_4 (
    .CK(senso_fianl_1_counted_exit), .RS(Reset), .out_3(up_counter_4_out_3), .out_4(up_counter_4_out_4),
    .out_5(up_counter_4_out_5), .out_6(up_counter_4_out_6), .out_7(up_counter_4_out_7),
    .out_8(up_counter_4_out_8), .out_9(up_counter_4_out_9), .out_10(up_counter_4_out_10));
  TERM2PROJECTADDERSUBTRACTOR_2__main Number_of_people_Counting_System (
    .CONTROL_BIT(1'b1), .in_3(up_counter_1_out_10), .in_4(up_counter_1_out_9), .in_5(up_counter_1_out_8),
    .in_6(up_counter_1_out_7), .in_7(up_counter_1_out_6), .in_8(up_counter_1_out_5),
    .in_9(up_counter_1_out_4), .in_2(Reset), .in_10(up_counter_1_out_3), .in_11(up_counter_2_out_10),
    .in_12(up_counter_2_out_9), .in_13(up_counter_2_out_8), .in_14(up_counter_2_out_7),
    .in_15(up_counter_2_out_6), .in_16(up_counter_2_out_5), .in_17(up_counter_2_out_4),
    .in_18(up_counter_2_out_3), .out_19(Number_of_people_Counting_System_out_19),
    .out_20(Number_of_people_Counting_System_out_20), .out_21(Number_of_people_Counting_System_out_21),
    .out_22(Number_of_people_Counting_System_out_22), .out_23(Number_of_people_Counting_System_out_23),
    .out_24(Number_of_people_Counting_System_out_24), .out_25(Number_of_people_Counting_System_out_25),
    .out_26(Number_of_people_Counting_System_out_26), .out_27(Number_of_people_Counting_System_out_27),
    .out_28(Number_of_people_Counting_System_out_28), .out_29(Number_of_people_Counting_System_out_29),
    .out_30(Number_of_people_Counting_System_out_30), .out_31(Number_of_people_Counting_System_out_31),
    .out_32(Number_of_people_Counting_System_out_32), .out_33(Number_of_people_Counting_System_out_33),
    .out_34(Number_of_people_Counting_System_out_34), .out_35(Number_of_people_Counting_System_out_35),
    .out_36(Number_of_people_Counting_System_out_36), .out_37(Number_of_people_Counting_System_out_37),
    .out_38(Number_of_people_Counting_System_out_38), .out_39(Number_of_people_Counting_System_out_39));
  numberofseats Number_of_seats_counting_system (
    .in_1(Reset), .in_2(1'b1), .in_3(up_counter_3_out_10), .in_4(up_counter_3_out_9),
    .in_5(up_counter_3_out_8), .in_6(up_counter_3_out_7), .in_7(up_counter_3_out_6),
    .in_8(up_counter_3_out_5), .in_9(up_counter_3_out_4), .in_10(up_counter_3_out_3),
    .in_11(up_counter_4_out_10), .in_12(up_counter_4_out_9), .in_13(up_counter_4_out_8),
    .in_14(up_counter_4_out_7), .in_15(up_counter_4_out_6), .in_16(up_counter_4_out_5),
    .in_17(up_counter_4_out_4), .in_18(up_counter_4_out_3), .out_19(Number_of_seats_counting_system_out_19),
    .out_20(Number_of_seats_counting_system_out_20), .out_21(Number_of_seats_counting_system_out_21),
    .out_22(Number_of_seats_counting_system_out_22), .out_23(Number_of_seats_counting_system_out_23),
    .out_24(Number_of_seats_counting_system_out_24), .out_25(Number_of_seats_counting_system_out_25),
    .out_26(Number_of_seats_counting_system_out_26), .out_27(Number_of_seats_counting_system_out_27),
    .out_28(Number_of_seats_counting_system_out_28), .out_29(Number_of_seats_counting_system_out_29),
    .out_30(Number_of_seats_counting_system_out_30), .out_31(Number_of_seats_counting_system_out_31),
    .out_32(Number_of_seats_counting_system_out_32), .out_33(Number_of_seats_counting_system_out_33),
    .out_34(Number_of_seats_counting_system_out_34), .out_35(Number_of_seats_counting_system_out_35),
    .out_36(Number_of_seats_counting_system_out_36), .out_37(Number_of_seats_counting_system_out_37),
    .out_38(Number_of_seats_counting_system_out_38), .out_39(Number_of_seats_counting_system_out_39));
  _7_Segment_Display u_7_segment_display_1 (
    .g(Number_of_people_Counting_System_out_25), .f(Number_of_people_Counting_System_out_24),
    .a(Number_of_people_Counting_System_out_19), .b(Number_of_people_Counting_System_out_20),
    .e(Number_of_people_Counting_System_out_23), .d(Number_of_people_Counting_System_out_22),
    .c(Number_of_people_Counting_System_out_21));  // open: dp
  _7_Segment_Display u_7_segment_display_2 (
    .g(Number_of_people_Counting_System_out_39), .f(Number_of_people_Counting_System_out_38),
    .a(Number_of_people_Counting_System_out_33), .b(Number_of_people_Counting_System_out_34),
    .e(Number_of_people_Counting_System_out_37), .d(Number_of_people_Counting_System_out_36),
    .c(Number_of_people_Counting_System_out_35));  // open: dp
  _7_Segment_Display u_7_segment_display_3 (
    .g(Number_of_seats_counting_system_out_25), .f(Number_of_seats_counting_system_out_24),
    .a(Number_of_seats_counting_system_out_19), .b(Number_of_seats_counting_system_out_20),
    .e(Number_of_seats_counting_system_out_23), .d(Number_of_seats_counting_system_out_22),
    .c(Number_of_seats_counting_system_out_21));  // open: dp
  _7_Segment_Display u_7_segment_display_4 (
    .g(Number_of_seats_counting_system_out_32), .f(Number_of_seats_counting_system_out_31),
    .a(Number_of_seats_counting_system_out_26), .b(Number_of_seats_counting_system_out_27),
    .e(Number_of_seats_counting_system_out_30), .d(Number_of_seats_counting_system_out_29),
    .c(Number_of_seats_counting_system_out_28));  // open: dp
  _7_Segment_Display u_7_segment_display_5 (
    .g(Number_of_seats_counting_system_out_39), .f(Number_of_seats_counting_system_out_38),
    .a(Number_of_seats_counting_system_out_33), .b(Number_of_seats_counting_system_out_34),
    .e(Number_of_seats_counting_system_out_37), .d(Number_of_seats_counting_system_out_36),
    .c(Number_of_seats_counting_system_out_35));  // open: dp
  _7_Segment_Display u_7_segment_display_6 (
    .g(Number_of_people_Counting_System_out_32), .f(Number_of_people_Counting_System_out_31),
    .a(Number_of_people_Counting_System_out_26), .b(Number_of_people_Counting_System_out_27),
    .e(Number_of_people_Counting_System_out_30), .d(Number_of_people_Counting_System_out_29),
    .c(Number_of_people_Counting_System_out_28));  // open: dp

  // Notes on the sheet:
  //   Entry
  //   Exit
  //   Number of People on the floor 
  //   Number of Free  Seats on the Floor 
endmodule

module SR_latch (
  input  R,
  input  S,
  output Q,
  output Q_prime
);

  nor nor_1 (Q, R, Q_prime);
  nor nor_2 (Q_prime, Q, S);
endmodule

module Dff (
  input  D,
  input  clk,
  output Q,
  output Q_prime
);

  wire nand_1_out, nand_2_out, not_1_out;

  not not_1 (not_1_out, D);
  nand nand_1 (nand_1_out, D, clk);
  nand nand_2 (nand_2_out, clk, not_1_out);
  nand nand_3 (Q, nand_1_out, Q_prime);
  nand nand_4 (Q_prime, Q, nand_2_out);
endmodule

module sensor_buffer (
  input  IR2,
  input  IR1,
  input  IR2_2,
  input  IR1_2,
  input  IR2_3,
  input  IR1_3,
  input  in_7
);

  wire and_1_out, and_2_out, and_3_out, and_4_out, and_5_out, and_6_out, and_7_out, and_8_out, and_9_out,
       and_10_out, and_11_out, and_12_out, and_13_out, and_14_out, and_15_out, and_16_out, and_17_out,
       and_18_out, and_19_out, and_20_out, and_21_out, and_22_out, and_23_out, and_24_out, and_25_out,
       Both_Triggered_out, dff_1_q, dff_1_q_prime, dff_2_q, dff_2_q_prime, dff_3_q, dff_3_q_prime, dff_4_q,
       dff_4_q_prime, dff_5_q_prime, dff_6_q_prime, dff_7_q, dff_7_q_prime, dff_8_q, dff_8_q_prime, dff_9_q,
       dff_9_q_prime, dff_10_q, dff_10_q_prime, dff_11_q_prime, dff_12_q_prime, dff_13_q_prime, dff_14_q,
       dff_14_q_prime, dff_15_q_prime, dff_16_q_prime, not_1_out, not_2_out, not_3_out, not_4_out, not_5_out,
       not_6_out, not_7_out, not_8_out, not_9_out, not_10_out, not_11_out, not_12_out, not_13_out,
       not_14_out, not_15_out, not_16_out, not_17_out, not_18_out, not_19_out, not_20_out, or_1_out,
       or_2_out, or_3_out, or_4_out, or_5_out, or_6_out, or_7_out, or_8_out, or_9_out, or_10_out, or_11_out,
       or_12_out, sr_latch_1_q, sr_latch_1_q_prime, sr_latch_2_q, sr_latch_3_q_prime, sr_latch_4_q,
       sr_latch_4_q_prime, sr_latch_5_q, sr_latch_6_q, sr_latch_7_q, sr_latch_8_q, sr_latch_9_q,
       sr_latch_9_q_prime, sr_latch_10_q, sr_latch_10_q_prime, undriven;

  not not_1 (not_1_out, IR2);
  not not_2 (not_2_out, IR1);
  and and_1 (and_1_out, IR1, not_1_out);
  and and_2 (and_2_out, not_2_out, IR2);
  not not_3 (not_3_out, IR2_3);
  not not_4 (not_4_out, IR1_3);
  or or_1 (or_1_out, and_1_out, dff_6_q_prime, undriven);
  or or_2 (or_2_out, and_2_out, dff_5_q_prime);
  and and_3 (and_3_out, IR1_3, not_3_out);
  and and_4 (and_4_out, not_4_out, IR2_3);
  Dff dff_1 (.D(IR1), .clk(or_1_out), .Q(dff_1_q), .Q_prime(dff_1_q_prime));
  Dff dff_2 (.D(IR2), .clk(or_2_out), .Q(dff_2_q), .Q_prime(dff_2_q_prime));
  Dff dff_3 (.D(IR1_3), .clk(and_3_out), .Q(dff_3_q), .Q_prime(dff_3_q_prime));
  Dff dff_4 (.D(IR2_3), .clk(and_4_out), .Q(dff_4_q), .Q_prime(dff_4_q_prime));
  not not_5 (not_5_out, dff_1_q_prime);
  not not_6 (not_6_out, dff_2_q_prime);
  not not_7 (not_7_out, dff_3_q_prime);
  SR_latch sr_latch_1 (.R(and_10_out), .S(dff_4_q), .Q(sr_latch_1_q), .Q_prime(sr_latch_1_q_prime));
  not not_8 (not_8_out, dff_4_q_prime);
  and and_5 (and_5_out, dff_1_q_prime, IR2);
  and and_6 (and_6_out, not_5_out, IR2);
  and and_7 (and_7_out, IR1, dff_2_q_prime);
  and and_8 (and_8_out, not_6_out, IR1);
  SR_latch sr_latch_2 (.R(and_9_out), .S(dff_3_q), .Q(sr_latch_2_q));  // open: Q_prime
  and and_9 (and_9_out, not_7_out, IR2_3);
  and and_10 (and_10_out, not_8_out, IR1_3);
  or or_3 (or_3_out, IR1, and_5_out);
  or or_4 (or_4_out, IR2, and_7_out);
  Dff dff_5 (.D(and_8_out), .clk(or_2_out), .Q_prime(dff_5_q_prime));  // open: Q
  or or_5 (or_5_out, sr_latch_2_q, and_9_out);
  not not_9 (not_9_out, IR2_3);
  or or_6 (or_6_out, sr_latch_1_q, and_10_out);
  SR_latch sr_latch_3 (.R(or_3_out), .S(dff_1_q), .Q_prime(sr_latch_3_q_prime));  // open: Q
  Dff dff_6 (.D(and_6_out), .clk(or_1_out), .Q_prime(dff_6_q_prime));  // open: Q
  and and_11 (and_11_out, IR1_3, not_9_out, or_6_out);
  SR_latch sr_latch_4 (.R(or_4_out), .S(dff_2_q), .Q(sr_latch_4_q), .Q_prime(sr_latch_4_q_prime));
  not not_10 (not_10_out, IR1_3);
  not not_11 (not_11_out, IR1);
  not not_12 (not_12_out, IR2);
  and and_12 (and_12_out, not_10_out, IR2_3, or_5_out);
  and and_13 (and_13_out, not_11_out, IR2, sr_latch_3_q_prime);
  and and_14 (and_14_out, IR1, not_12_out, sr_latch_4_q_prime);
  or or_7 (or_7_out, IR1_2, dff_12_q_prime);
  or or_8 (or_8_out, IR2_2, dff_13_q_prime);
  Dff dff_7 (.D(IR1_2), .clk(or_7_out), .Q(dff_7_q), .Q_prime(dff_7_q_prime));
  Dff dff_8 (.D(IR2_2), .clk(or_8_out), .Q(dff_8_q), .Q_prime(dff_8_q_prime));
  not not_13 (not_13_out, IR2_2);
  not not_14 (not_14_out, IR1_2);
  not not_15 (not_15_out, dff_7_q_prime);
  not not_16 (not_16_out, dff_8_q_prime);
  and and_15 (and_15_out, IR1_2, not_13_out);
  and and_16 (and_16_out, not_14_out, IR2_2);
  or or_9 (or_9_out, and_16_out, dff_16_q_prime);
  and and_17 (and_17_out, IR2_2, not_15_out);
  Dff dff_9 (.D(dff_8_q), .clk(or_8_out), .Q(dff_9_q), .Q_prime(dff_9_q_prime));
  SR_latch sr_latch_5 (.R(dff_9_q_prime), .S(dff_8_q), .Q(sr_latch_5_q));  // open: Q_prime
  and and_18 (and_18_out, not_16_out, IR1_2);
  or or_10 (or_10_out, and_15_out, dff_15_q_prime);
  Dff dff_10 (.D(IR2_2), .clk(or_9_out), .Q(dff_10_q), .Q_prime(dff_10_q_prime));
  Dff dff_11 (.D(dff_7_q), .clk(or_7_out), .Q_prime(dff_11_q_prime));  // open: Q
  SR_latch sr_latch_6 (.R(dff_11_q_prime), .S(dff_7_q), .Q(sr_latch_6_q));  // open: Q_prime
  Dff dff_12 (.D(and_17_out), .clk(or_7_out), .Q_prime(dff_12_q_prime));  // open: Q
  Dff dff_13 (.D(and_18_out), .clk(or_8_out), .Q_prime(dff_13_q_prime));  // open: Q
  Dff dff_14 (.D(IR1_2), .clk(or_10_out), .Q(dff_14_q), .Q_prime(dff_14_q_prime));
  not not_17 (not_17_out, dff_14_q_prime);
  not not_18 (not_18_out, dff_10_q_prime);
  SR_latch sr_latch_7 (.R(and_23_out), .S(sr_latch_6_q), .Q(sr_latch_7_q));  // open: Q_prime
  SR_latch sr_latch_8 (.R(and_23_out), .S(sr_latch_5_q), .Q(sr_latch_8_q));  // open: Q_prime
  and and_19 (and_19_out, IR2_2, dff_14_q_prime);
  and and_20 (and_20_out, not_17_out, IR2_2);
  and and_21 (and_21_out, IR1_2, dff_10_q_prime);
  and and_22 (and_22_out, not_18_out, IR1_2);
  or or_11 (or_11_out, and_19_out, IR1_2);
  Dff dff_15 (.D(and_20_out), .clk(or_10_out), .Q_prime(dff_15_q_prime));  // open: Q
  or or_12 (or_12_out, and_21_out, IR2_2);
  Dff dff_16 (.D(and_22_out), .clk(or_9_out), .Q_prime(dff_16_q_prime));  // open: Q
  and Both_Triggered (Both_Triggered_out, sr_latch_7_q, sr_latch_8_q);
  SR_latch sr_latch_9 (.R(or_11_out), .S(dff_14_q), .Q(sr_latch_9_q), .Q_prime(sr_latch_9_q_prime));
  SR_latch sr_latch_10 (.R(or_12_out), .S(dff_10_q), .Q(sr_latch_10_q), .Q_prime(sr_latch_10_q_prime));
  and and_23 (and_23_out, in_7, Both_Triggered_out);
  not not_19 (not_19_out, IR1_2);
  not not_20 (not_20_out, IR2_2);
  and and_24 (and_24_out, not_19_out, IR2_2, sr_latch_9_q_prime, Both_Triggered_out);
  and and_25 (and_25_out, IR1_2, not_20_out, sr_latch_10_q_prime, Both_Triggered_out);

  // Notes on the sheet:
  //   Exit
  //   Enter
  //   Enter
  //   Exit
  //   Enter
  //   Exit
endmodule

module senso_fianl (
  input  in_1,
  input  LS1,
  input  LS2,
  input  LS3,
  input  LS4,
  output Counted_Enter,
  output Counted_Exit
);

  wire and_1_out, and_2_out, and_3_out, and_4_out, and_5_out, and_6_out, and_7_out, and_8_out, and_9_out,
       and_10_out, and_11_out, and_12_out, and_13_out, and_14_out, and_15_out, and_16_out, and_17_out,
       and_18_out, and_19_out, and_20_out, and_21_out, and_22_out, and_23_out, and_24_out, and_25_out,
       and_26_out, and_27_out, and_28_out, and_29_out, and_30_out, and_31_out, and_32_out,
       Both_Triggered_2_out, Both_Triggered_3_out, Both_Triggered_out, dff_1_q, dff_1_q_prime, dff_2_q,
       dff_2_q_prime, dff_3_q, dff_3_q_prime, dff_4_q, dff_4_q_prime, dff_5_q, dff_5_q_prime, dff_6_q,
       dff_6_q_prime, dff_7_q_prime, dff_8_q_prime, dff_9_q_prime, dff_10_q_prime, dff_11_q_prime,
       dff_12_q_prime, dff_13_q_prime, dff_14_q_prime, dff_15_q_prime, dff_16_q_prime, dff_17_q_prime,
       dff_18_q_prime, dff_19_q, dff_19_q_prime, dff_20_q, dff_20_q_prime, dff_21_q_prime, dff_22_q_prime,
       dff_23_q, dff_23_q_prime, dff_24_q, dff_24_q_prime, dff_25_q, dff_25_q_prime, dff_26_q,
       dff_26_q_prime, dff_27_q_prime, dff_28_q_prime, dff_29_q, dff_29_q_prime, dff_30_q, dff_30_q_prime,
       dff_31_q, dff_31_q_prime, dff_32_q, dff_32_q_prime, dff_33_q_prime, dff_34_q_prime, dff_35_q,
       dff_35_q_prime, dff_36_q, dff_36_q_prime, not_1_out, not_2_out, not_3_out, not_4_out, not_5_out,
       not_6_out, not_7_out, not_8_out, not_9_out, not_10_out, not_11_out, not_12_out, not_13_out,
       not_14_out, not_15_out, not_16_out, not_17_out, not_18_out, not_19_out, not_20_out, not_21_out,
       not_22_out, not_23_out, not_24_out, not_25_out, not_26_out, or_1_out, or_2_out, or_3_out, or_4_out,
       or_5_out, or_6_out, or_7_out, or_8_out, or_9_out, or_10_out, or_11_out, or_12_out, or_13_out,
       or_14_out, or_15_out, or_16_out, or_17_out, or_18_out, or_19_out, or_20_out, or_21_out, or_22_out,
       or_23_out, or_24_out, or_25_out, or_26_out, or_27_out, or_28_out, or_29_out, or_30_out, sr_latch_1_q,
       sr_latch_2_q, sr_latch_3_q, sr_latch_4_q, sr_latch_5_q, sr_latch_6_q, sr_latch_7_q, sr_latch_8_q,
       sr_latch_9_q, sr_latch_10_q, sr_latch_11_q, sr_latch_12_q, sr_latch_13_q_prime, sr_latch_14_q_prime,
       sr_latch_15_q, sr_latch_16_q, sr_latch_17_q_prime, sr_latch_18_q_prime, sr_latch_19_q, sr_latch_20_q,
       sr_latch_21_q_prime, sr_latch_22_q_prime, sr_latch_23_q_prime, sr_latch_24_q_prime, sr_latch_25_q,
       sr_latch_26_q;

  or or_1 (or_1_out, LS1, dff_8_q_prime);
  or or_2 (or_2_out, LS2, dff_10_q_prime);
  or or_3 (or_3_out, LS2, dff_12_q_prime);
  or or_4 (or_4_out, LS3, dff_14_q_prime);
  Dff dff_1 (.D(LS1), .clk(or_1_out), .Q(dff_1_q), .Q_prime(dff_1_q_prime));
  Dff dff_2 (.D(LS2), .clk(or_2_out), .Q(dff_2_q), .Q_prime(dff_2_q_prime));
  Dff dff_3 (.D(LS2), .clk(or_3_out), .Q(dff_3_q), .Q_prime(dff_3_q_prime));
  Dff dff_4 (.D(LS3), .clk(or_4_out), .Q(dff_4_q), .Q_prime(dff_4_q_prime));
  Dff dff_5 (.D(LS3), .clk(or_5_out), .Q(dff_5_q), .Q_prime(dff_5_q_prime));
  or or_5 (or_5_out, LS3, dff_16_q_prime);
  Dff dff_6 (.D(LS4), .clk(or_6_out), .Q(dff_6_q), .Q_prime(dff_6_q_prime));
  or or_6 (or_6_out, LS4, dff_18_q_prime);
  not not_1 (not_1_out, LS2);
  not not_2 (not_2_out, LS1);
  not not_3 (not_3_out, dff_1_q_prime);
  not not_4 (not_4_out, dff_2_q_prime);
  not not_5 (not_5_out, dff_3_q_prime);
  not not_6 (not_6_out, dff_4_q_prime);
  not not_7 (not_7_out, dff_5_q_prime);
  not not_8 (not_8_out, dff_6_q_prime);
  and and_1 (and_1_out, LS1, not_1_out);
  and and_2 (and_2_out, not_2_out, LS2);
  and and_3 (and_3_out, not_3_out, LS2);
  and and_4 (and_4_out, not_4_out, LS1);
  and and_5 (and_5_out, not_5_out, LS3);
  and and_6 (and_6_out, not_6_out, LS2);
  and and_7 (and_7_out, not_7_out, LS4);
  and and_8 (and_8_out, not_8_out, LS3);
  or or_7 (or_7_out, and_1_out, dff_21_q_prime);
  or or_8 (or_8_out, and_2_out, dff_22_q_prime);
  Dff dff_7 (.D(dff_1_q), .clk(or_1_out), .Q_prime(dff_7_q_prime));  // open: Q
  SR_latch sr_latch_1 (.R(dff_7_q_prime), .S(dff_1_q), .Q(sr_latch_1_q));  // open: Q_prime
  Dff dff_8 (.D(and_3_out), .clk(or_1_out), .Q_prime(dff_8_q_prime));  // open: Q
  Dff dff_9 (.D(dff_2_q), .clk(or_2_out), .Q_prime(dff_9_q_prime));  // open: Q
  SR_latch sr_latch_2 (.R(dff_9_q_prime), .S(dff_2_q), .Q(sr_latch_2_q));  // open: Q_prime
  Dff dff_10 (.D(and_4_out), .clk(or_2_out), .Q_prime(dff_10_q_prime));  // open: Q
  Dff dff_11 (.D(dff_3_q), .clk(or_3_out), .Q_prime(dff_11_q_prime));  // open: Q
  SR_latch sr_latch_3 (.R(dff_11_q_prime), .S(dff_3_q), .Q(sr_latch_3_q));  // open: Q_prime
  Dff dff_12 (.D(and_5_out), .clk(or_3_out), .Q_prime(dff_12_q_prime));  // open: Q
  Dff dff_13 (.D(dff_4_q), .clk(or_4_out), .Q_prime(dff_13_q_prime));  // open: Q
  SR_latch sr_latch_4 (.R(dff_13_q_prime), .S(dff_4_q), .Q(sr_latch_4_q));  // open: Q_prime
  Dff dff_14 (.D(and_6_out), .clk(or_4_out), .Q_prime(dff_14_q_prime));  // open: Q
  Dff dff_15 (.D(dff_5_q), .clk(or_5_out), .Q_prime(dff_15_q_prime));  // open: Q
  SR_latch sr_latch_5 (.R(dff_15_q_prime), .S(dff_5_q), .Q(sr_latch_5_q));  // open: Q_prime
  Dff dff_16 (.D(and_7_out), .clk(or_5_out), .Q_prime(dff_16_q_prime));  // open: Q
  Dff dff_17 (.D(dff_6_q), .clk(or_6_out), .Q_prime(dff_17_q_prime));  // open: Q
  SR_latch sr_latch_6 (.R(dff_17_q_prime), .S(dff_6_q), .Q(sr_latch_6_q));  // open: Q_prime
  Dff dff_18 (.D(and_8_out), .clk(or_6_out), .Q_prime(dff_18_q_prime));  // open: Q
  Dff dff_19 (.D(LS1), .clk(or_7_out), .Q(dff_19_q), .Q_prime(dff_19_q_prime));
  not not_9 (not_9_out, dff_19_q_prime);
  Dff dff_20 (.D(LS2), .clk(or_8_out), .Q(dff_20_q), .Q_prime(dff_20_q_prime));
  not not_10 (not_10_out, dff_20_q_prime);
  SR_latch sr_latch_7 (.R(in_1), .S(sr_latch_1_q), .Q(sr_latch_7_q));  // open: Q_prime
  SR_latch sr_latch_8 (.R(in_1), .S(sr_latch_2_q), .Q(sr_latch_8_q));  // open: Q_prime
  SR_latch sr_latch_9 (.R(in_1), .S(sr_latch_3_q), .Q(sr_latch_9_q));  // open: Q_prime
  SR_latch sr_latch_10 (.R(in_1), .S(sr_latch_4_q), .Q(sr_latch_10_q));  // open: Q_prime
  SR_latch sr_latch_11 (.R(in_1), .S(sr_latch_5_q), .Q(sr_latch_11_q));  // open: Q_prime
  SR_latch sr_latch_12 (.R(in_1), .S(sr_latch_6_q), .Q(sr_latch_12_q));  // open: Q_prime
  and and_9 (and_9_out, LS2, dff_19_q_prime);
  and and_10 (and_10_out, not_9_out, LS2);
  and and_11 (and_11_out, LS1, dff_20_q_prime);
  and and_12 (and_12_out, not_10_out, LS1);
  or or_9 (or_9_out, LS1, and_9_out);
  Dff dff_21 (.D(and_10_out), .clk(or_7_out), .Q_prime(dff_21_q_prime));  // open: Q
  or or_10 (or_10_out, LS2, and_11_out);
  Dff dff_22 (.D(and_12_out), .clk(or_8_out), .Q_prime(dff_22_q_prime));  // open: Q
  and Both_Triggered (Both_Triggered_out, sr_latch_7_q, sr_latch_8_q);
  and Both_Triggered_2 (Both_Triggered_2_out, sr_latch_9_q, sr_latch_10_q);
  and Both_Triggered_3 (Both_Triggered_3_out, sr_latch_11_q, sr_latch_12_q);
  SR_latch sr_latch_13 (.R(or_9_out), .S(dff_19_q), .Q_prime(sr_latch_13_q_prime));  // open: Q
  SR_latch sr_latch_14 (.R(or_10_out), .S(dff_20_q), .Q_prime(sr_latch_14_q_prime));  // open: Q
  and and_13 (and_13_out, LS4, Both_Triggered_out, sr_latch_13_q_prime);
  and and_14 (and_14_out, LS1, Both_Triggered_out, sr_latch_14_q_prime);
  or or_11 (or_11_out, and_14_out, not_12_out);
  Dff dff_23 (.D(and_13_out), .clk(or_12_out), .Q(dff_23_q), .Q_prime(dff_23_q_prime));
  or or_12 (or_12_out, and_13_out, not_11_out);
  not not_11 (not_11_out, dff_23_q_prime);
  Dff dff_24 (.D(and_14_out), .clk(or_11_out), .Q(dff_24_q), .Q_prime(dff_24_q_prime));
  not not_12 (not_12_out, dff_24_q_prime);
  and and_15 (and_15_out, Both_Triggered_out, Both_Triggered_2_out, Both_Triggered_3_out);
  SR_latch sr_latch_15 (.R(or_13_out), .S(dff_23_q), .Q(sr_latch_15_q));  // open: Q_prime
  or or_13 (or_13_out, sr_latch_24_q_prime, in_1);
  or or_14 (or_14_out, sr_latch_21_q_prime, in_1);
  SR_latch sr_latch_16 (.R(or_14_out), .S(dff_24_q), .Q(sr_latch_16_q));  // open: Q_prime
  not not_13 (not_13_out, LS3);
  not not_14 (not_14_out, LS2);
  and and_16 (and_16_out, LS2, not_13_out);
  and and_17 (and_17_out, not_14_out, LS3);
  or or_15 (or_15_out, and_16_out, dff_27_q_prime);
  or or_16 (or_16_out, and_17_out, dff_28_q_prime);
  Dff dff_25 (.D(LS2), .clk(or_15_out), .Q(dff_25_q), .Q_prime(dff_25_q_prime));
  Dff dff_26 (.D(LS3), .clk(or_16_out), .Q(dff_26_q), .Q_prime(dff_26_q_prime));
  not not_15 (not_15_out, dff_25_q_prime);
  and and_18 (and_18_out, LS2, dff_26_q_prime);
  not not_16 (not_16_out, dff_26_q_prime);
  and and_19 (and_19_out, not_16_out, LS2);
  and and_20 (and_20_out, LS3, dff_25_q_prime);
  and and_21 (and_21_out, not_15_out, LS3);
  or or_17 (or_17_out, LS2, and_20_out);
  Dff dff_27 (.D(and_21_out), .clk(or_15_out), .Q_prime(dff_27_q_prime));  // open: Q
  or or_18 (or_18_out, LS3, and_18_out);
  Dff dff_28 (.D(and_19_out), .clk(or_16_out), .Q_prime(dff_28_q_prime));  // open: Q
  SR_latch sr_latch_17 (.R(or_17_out), .S(dff_25_q), .Q_prime(sr_latch_17_q_prime));  // open: Q
  SR_latch sr_latch_18 (.R(or_18_out), .S(dff_26_q), .Q_prime(sr_latch_18_q_prime));  // open: Q
  and and_22 (and_22_out, LS4, sr_latch_17_q_prime, Both_Triggered_2_out);
  or or_19 (or_19_out, and_22_out, not_17_out);
  and and_23 (and_23_out, LS1, Both_Triggered_2_out, sr_latch_18_q_prime);
  Dff dff_29 (.D(and_22_out), .clk(or_19_out), .Q(dff_29_q), .Q_prime(dff_29_q_prime));
  not not_17 (not_17_out, dff_29_q_prime);
  Dff dff_30 (.D(and_23_out), .clk(or_20_out), .Q(dff_30_q), .Q_prime(dff_30_q_prime));
  or or_20 (or_20_out, and_23_out, not_18_out);
  not not_18 (not_18_out, dff_30_q_prime);
  or or_21 (or_21_out, sr_latch_24_q_prime, in_1);
  or or_22 (or_22_out, sr_latch_21_q_prime, in_1);
  SR_latch sr_latch_19 (.R(or_21_out), .S(dff_29_q), .Q(sr_latch_19_q));  // open: Q_prime
  SR_latch sr_latch_20 (.R(or_22_out), .S(dff_30_q), .Q(sr_latch_20_q));  // open: Q_prime
  not not_19 (not_19_out, LS4);
  not not_20 (not_20_out, LS3);
  and and_24 (and_24_out, LS3, not_19_out);
  and and_25 (and_25_out, not_20_out, LS4);
  or or_23 (or_23_out, and_24_out, dff_33_q_prime);
  or or_24 (or_24_out, and_25_out, dff_34_q_prime);
  Dff dff_31 (.D(LS3), .clk(or_23_out), .Q(dff_31_q), .Q_prime(dff_31_q_prime));
  Dff dff_32 (.D(LS4), .clk(or_24_out), .Q(dff_32_q), .Q_prime(dff_32_q_prime));
  not not_21 (not_21_out, dff_31_q_prime);
  not not_22 (not_22_out, dff_32_q_prime);
  and and_26 (and_26_out, LS4, dff_31_q_prime);
  and and_27 (and_27_out, not_21_out, LS4);
  and and_28 (and_28_out, LS3, dff_32_q_prime);
  and and_29 (and_29_out, not_22_out, LS3);
  SR_latch sr_latch_21 (.R(LS4), .S(LS1), .Q_prime(sr_latch_21_q_prime));  // open: Q
  or or_25 (or_25_out, LS3, and_26_out);
  Dff dff_33 (.D(and_27_out), .clk(or_23_out), .Q_prime(dff_33_q_prime));  // open: Q
  or or_26 (or_26_out, LS4, and_28_out);
  Dff dff_34 (.D(and_29_out), .clk(or_24_out), .Q_prime(dff_34_q_prime));  // open: Q
  SR_latch sr_latch_22 (.R(or_25_out), .S(dff_31_q), .Q_prime(sr_latch_22_q_prime));  // open: Q
  SR_latch sr_latch_23 (.R(or_26_out), .S(dff_32_q), .Q_prime(sr_latch_23_q_prime));  // open: Q
  and and_30 (and_30_out, sr_latch_19_q, sr_latch_15_q, sr_latch_22_q_prime, Both_Triggered_3_out);
  and and_31 (and_31_out, LS1, Both_Triggered_3_out, sr_latch_23_q_prime);
  Dff dff_35 (.D(and_30_out), .clk(or_27_out), .Q(dff_35_q), .Q_prime(dff_35_q_prime));
  or or_27 (or_27_out, and_30_out, not_24_out);
  Dff dff_36 (.D(and_31_out), .clk(or_28_out), .Q(dff_36_q), .Q_prime(dff_36_q_prime));
  or or_28 (or_28_out, and_31_out, not_23_out);
  not not_23 (not_23_out, dff_36_q_prime);
  SR_latch sr_latch_24 (.R(LS1), .S(LS4), .Q_prime(sr_latch_24_q_prime));  // open: Q
  not not_24 (not_24_out, dff_35_q_prime);
  SR_latch sr_latch_25 (.R(or_29_out), .S(dff_36_q), .Q(sr_latch_25_q));  // open: Q_prime
  or or_29 (or_29_out, sr_latch_21_q_prime, in_1);
  or or_30 (or_30_out, sr_latch_24_q_prime, in_1);
  not not_25 (not_25_out, LS4);
  not not_26 (not_26_out, LS1);
  SR_latch sr_latch_26 (.R(or_30_out), .S(dff_35_q), .Q(sr_latch_26_q));  // open: Q_prime
  and and_32 (and_32_out, sr_latch_25_q, sr_latch_16_q, sr_latch_20_q);
  and and_33 (Counted_Enter, not_26_out, sr_latch_26_q, and_15_out);
  and and_34 (Counted_Exit, not_25_out, and_32_out, and_15_out);

  // Notes on the sheet:
  //   LS3
  //   LS4
  //   LS1
  //   LS2
  //   IR2_IR3
  //   IR1_IR2
  //   IR3_IR4
  //   Exit
  //   Enter
  //   Enter
  //   Exit
  //   All_Circuit_Reset
  //   All Entry
  //   Enter
  //   Exit
  //   All Exit 
endmodule

module numberofseats (
  input  in_1,
  input  in_2,
  input  in_3,
  input  in_4,
  input  in_5,
  input  in_6,
  input  in_7,
  input  in_8,
  input  in_9,
  input  in_10,
  input  in_11,
  input  in_12,
  input  in_13,
  input  in_14,
  input  in_15,
  input  in_16,
  input  in_17,
  input  in_18,
  output out_19,
  output out_20,
  output out_21,
  output out_22,
  output out_23,
  output out_24,
  output out_25,
  output out_26,
  output out_27,
  output out_28,
  output out_29,
  output out_30,
  output out_31,
  output out_32,
  output out_33,
  output out_34,
  output out_35,
  output out_36,
  output out_37,
  output out_38,
  output out_39
);

  wire as3_1_out_19, as3_1_out_20, as3_1_out_21, as3_1_out_22, as3_1_out_23, as3_1_out_24, as3_1_out_25,
       as3_1_out_26, as3_2_out_19, as3_2_out_20, as3_2_out_21, as3_2_out_22, as3_2_out_23, as3_2_out_24,
       as3_2_out_25, as3_2_out_26, n8bit7segment_1_out_9, n8bit7segment_1_out_10, n8bit7segment_1_out_11,
       n8bit7segment_1_out_12, n8bit7segment_1_out_13, n8bit7segment_1_out_14, n8bit7segment_1_out_15,
       n8bit7segment_1_out_16, n8bit7segment_1_out_17, n8bit7segment_1_out_18, n8bit7segment_1_out_19,
       n8bit7segment_1_out_20;

  AS3 as3_1 (
    .in_1(in_2), .in_3(in_3), .in_4(in_11), .in_5(in_4), .in_6(in_12), .in_7(in_5), .in_8(in_13),
    .in_9(in_6), .in_10(in_14), .in_11(in_7), .in_12(in_15), .in_13(in_8), .in_14(in_16), .in_15(in_9),
    .in_16(in_17), .in_17(in_10), .in_18(in_18), .out_19(as3_1_out_19), .out_20(as3_1_out_20),
    .out_21(as3_1_out_21), .out_22(as3_1_out_22), .out_23(as3_1_out_23), .out_24(as3_1_out_24),
    .out_25(as3_1_out_25), .out_26(as3_1_out_26), .in_2(in_1));  // open: out_27
  AS3 as3_2 (
    .in_1(in_2), .in_3(1'b0), .in_4(as3_1_out_19), .in_5(1'b0), .in_6(as3_1_out_20), .in_7(1'b0),
    .in_8(as3_1_out_21), .in_9(1'b0), .in_10(as3_1_out_22), .in_11(1'b1), .in_12(as3_1_out_23), .in_13(1'b1),
    .in_14(as3_1_out_24), .in_15(1'b1), .in_16(as3_1_out_25), .in_17(1'b0), .in_18(as3_1_out_26),
    .out_19(as3_2_out_19), .out_20(as3_2_out_20), .out_21(as3_2_out_21), .out_22(as3_2_out_22),
    .out_23(as3_2_out_23), .out_24(as3_2_out_24), .out_25(as3_2_out_25), .out_26(as3_2_out_26), .in_2(in_1));  // open: out_27
  _8bit7segment u_8bit7segment_1 (
    .in_1(as3_2_out_19), .in_2(as3_2_out_20), .in_3(as3_2_out_21), .in_4(as3_2_out_22), .in_5(as3_2_out_23),
    .in_6(as3_2_out_24), .in_7(as3_2_out_25), .in_8(as3_2_out_26), .out_9(n8bit7segment_1_out_9),
    .out_10(n8bit7segment_1_out_10), .out_11(n8bit7segment_1_out_11), .out_12(n8bit7segment_1_out_12),
    .out_13(n8bit7segment_1_out_13), .out_14(n8bit7segment_1_out_14), .out_15(n8bit7segment_1_out_15),
    .out_16(n8bit7segment_1_out_16), .out_17(n8bit7segment_1_out_17), .out_18(n8bit7segment_1_out_18),
    .out_19(n8bit7segment_1_out_19), .out_20(n8bit7segment_1_out_20));
  _7SEGMENT u_7segment_1 (
    .E(in_2), .S3(n8bit7segment_1_out_12), .a(out_19), .S2(n8bit7segment_1_out_11),
    .S1(n8bit7segment_1_out_10), .S0(n8bit7segment_1_out_9), .b(out_20), .c(out_21), .d(out_22),
    .e_2(out_23), .f(out_24), .g(out_25));
  _7SEGMENT u_7segment_2 (
    .E(in_2), .S3(n8bit7segment_1_out_16), .a(out_26), .S2(n8bit7segment_1_out_15),
    .S1(n8bit7segment_1_out_14), .S0(n8bit7segment_1_out_13), .b(out_27), .c(out_28), .d(out_29),
    .e_2(out_30), .f(out_31), .g(out_32));
  _7SEGMENT u_7segment_3 (
    .E(in_2), .S3(n8bit7segment_1_out_20), .a(out_33), .S2(n8bit7segment_1_out_19),
    .S1(n8bit7segment_1_out_18), .S0(n8bit7segment_1_out_17), .b(out_34), .c(out_35), .d(out_36),
    .e_2(out_37), .f(out_38), .g(out_39));
endmodule
