// Logisim project TERM2PROJECTADDERSUBTRACTOR[2].circ as structural Verilog: 8 circuits, main circuit main
module main (
  input  CONTROL_BIT,
  input  in_2,
  input  in_3,
  input  in_4,
  input  in_5,
  input  in_6,
  input  in_7,
  input  in_8,
  input  in_9,
  input  in_10,
  input  in_11,
  input  in_12,
  input  in_13,
  input  in_14,
  input  in_15,
  input  in_16,
  input  in_17,
  input  in_18,
  output out_19,
  output out_20,
  output out_21,
  output out_22,
  output out_23,
  output out_24,
  output out_25,
  output out_26,
  output out_27,
  output out_28,
  output out_29,
  output out_30,
  output out_31,
  output out_32,
  output out_33,
  output out_34,
  output out_35,
  output out_36,
  output out_37,
  output out_38,
  output out_39
);

  wire and_1_out, as3_1_out_19, as3_1_out_20, as3_1_out_21, as3_1_out_22, as3_1_out_23, as3_1_out_24,
       as3_1_out_25, as3_1_out_26, as3_1_out_27, comparator_1_eq, n8bit7segment_1_out_9,
       n8bit7segment_1_out_10, n8bit7segment_1_out_11, n8bit7segment_1_out_12, n8bit7segment_1_out_13,
       n8bit7segment_1_out_14, n8bit7segment_1_out_15, n8bit7segment_1_out_16, n8bit7segment_1_out_17,
       n8bit7segment_1_out_18, n8bit7segment_1_out_19, n8bit7segment_1_out_20, not_1_out, not_2_out;

  AS3 as3_1 (
    .in_1(CONTROL_BIT), .in_3(in_3), .in_4(in_11), .in_5(in_4), .in_6(in_12), .in_7(in_5), .in_8(in_13),
    .in_9(in_6), .in_10(in_14), .in_11(in_7), .in_12(in_15), .in_13(in_8), .in_14(in_16), .in_15(in_9),
    .in_16(in_17), .in_17(in_10), .in_18(in_18), .out_19(as3_1_out_19), .out_20(as3_1_out_20),
    .out_21(as3_1_out_21), .out_22(as3_1_out_22), .out_23(as3_1_out_23), .out_24(as3_1_out_24),
    .out_25(as3_1_out_25), .out_26(as3_1_out_26), .out_27(as3_1_out_27), .in_2(in_2));
  not not_1 (not_1_out, CONTROL_BIT);
  Comparator #(.width(1)) comparator_1 (.a(as3_1_out_27), .b(1'b1), .eq(comparator_1_eq));  // open: gt, lt
  _8bit7segment u_8bit7segment_1 (
    .in_1(as3_1_out_19), .in_2(as3_1_out_20), .in_3(as3_1_out_21), .in_4(as3_1_out_22), .in_5(as3_1_out_23),
    .in_6(as3_1_out_24), .in_7(as3_1_out_25), .in_8(as3_1_out_26), .out_9(n8bit7segment_1_out_9),
    .out_10(n8bit7segment_1_out_10), .out_11(n8bit7segment_1_out_11), .out_12(n8bit7segment_1_out_12),
    .out_13(n8bit7segment_1_out_13), .out_14(n8bit7segment_1_out_14), .out_15(n8bit7segment_1_out_15),
    .out_16(n8bit7segment_1_out_16), .out_17(n8bit7segment_1_out_17), .out_18(n8bit7segment_1_out_18),
    .out_19(n8bit7segment_1_out_19), .out_20(n8bit7segment_1_out_20));
  _7SEGMENT u_7segment_1 (
    .E(not_2_out), .S3(n8bit7segment_1_out_12), .a(out_19), .S2(n8bit7segment_1_out_11),
    .S1(n8bit7segment_1_out_10), .S0(n8bit7segment_1_out_9), .b(out_20), .c(out_21), .d(out_22),
    .e_2(out_23), .f(out_24), .g(out_25));
  _7SEGMENT u_7segment_2 (
    .E(not_2_out), .S3(n8bit7segment_1_out_20), .a(out_33), .S2(n8bit7segment_1_out_19),
    .S1(n8bit7segment_1_out_18), .S0(n8bit7segment_1_out_17), .b(out_34), .c(out_35), .d(out_36),
    .e_2(out_37), .f(out_38), .g(out_39));
  and and_1 (and_1_out, comparator_1_eq, not_1_out);
  _7SEGMENT u_7segment_3 (
    .E(not_2_out), .S3(n8bit7segment_1_out_16), .a(out_26), .S2(n8bit7segment_1_out_15),
    .S1(n8bit7segment_1_out_14), .S0(n8bit7segment_1_out_13), .b(out_27), .c(out_28), .d(out_29),
    .e_2(out_30), .f(out_31), .g(out_32));
  not not_2 (not_2_out, and_1_out);

  // Notes on the sheet:
  //   RESET
  //   INPUT BITS A
  //   INPUT BITS B
  //                              COMPARATOR
  //                                          7 SEGMENT DISPLAY 1
  //                                    7 SEGMENT DISPLAY 2
  //                                    7 SEGMENT DISPLAY 3
endmodule

module FA (
  input  Cin,
  input  x,
  input  y,
  output S,
  output Cout
);

  wire ha_1_out_3, ha_1_out_4, ha_2_out_4;

  HA ha_1 (.in_1(x), .in_2(y), .out_3(ha_1_out_3), .out_4(ha_1_out_4));
  HA ha_2 (.in_1(Cin), .in_2(ha_1_out_3), .out_3(S), .out_4(ha_2_out_4));
  or or_1 (Cout, ha_2_out_4, ha_1_out_4);
endmodule

module HA (
  input  in_1,
  input  in_2,
  output out_3,
  output out_4
);

  xor xor_1 (out_3, in_1, in_2);
  and and_1 (out_4, in_2, in_1);
endmodule

module AS (
  input  M,
  input  A0,
  input  B0,
  input  A1,
  input  B1,
  input  A2,
  input  B2,
  input  A3,
  input  B3,
  output S0,
  output S1,
  output S2,
  output S3,
  output C4
);

  wire fa_1_cout, fa_2_cout, fa_3_cout, xor_1_out, xor_2_out, xor_3_out, xor_4_out;

  xor xor_1 (xor_1_out, M, B0);
  xor xor_2 (xor_2_out, M, B1);
  xor xor_3 (xor_3_out, M, B3);
  xor xor_4 (xor_4_out, M, B2);
  FA fa_1 (.Cin(A0), .x(xor_1_out), .y(M), .S(S0), .Cout(fa_1_cout));
  FA fa_2 (.Cin(A1), .x(xor_2_out), .y(fa_1_cout), .S(S1), .Cout(fa_2_cout));
  FA fa_3 (.Cin(A2), .x(xor_4_out), .y(fa_2_cout), .S(S2), .Cout(fa_3_cout));
  FA fa_4 (.Cin(A3), .x(xor_3_out), .y(fa_3_cout), .S(S3), .Cout(C4));
endmodule

module AS3 (
  input  in_1,
  input  in_2,
  input  in_3,
  input  in_4,
  input  in_5,
  input  in_6,
  input  in_7,
  input  in_8,
  input  in_9,
  input  in_10,
  input  in_11,
  input  in_12,
  input  in_13,
  input  in_14,
  input  in_15,
  input  in_16,
  input  in_17,
  input  in_18,
  output out_19,
  output out_20,
  output out_21,
  output out_22,
  output out_23,
  output out_24,
  output out_25,
  output out_26,
  output out_27
);

  wire and_1_out, and_2_out, and_3_out, and_4_out, and_5_out, and_6_out, and_7_out, and_8_out, and_9_out,
       and_10_out, and_11_out, and_12_out, and_13_out, and_14_out, and_15_out, and_16_out, and_17_out,
       fa_1_cout, fa_2_cout, fa_3_cout, fa_4_cout, fa_5_cout, fa_6_cout, fa_7_cout, not_1_out, xor_1_out,
       xor_2_out, xor_3_out, xor_4_out, xor_5_out, xor_6_out, xor_7_out, xor_8_out;

  not not_1 (not_1_out, in_2);
  xor xor_1 (xor_1_out, in_1, in_4);
  xor xor_2 (xor_2_out, in_1, in_6);
  xor xor_3 (xor_3_out, in_1, in_8);
  xor xor_4 (xor_4_out, in_1, in_10);
  xor xor_5 (xor_5_out, in_1, in_12);
  xor xor_6 (xor_6_out, in_1, in_14);
  xor xor_7 (xor_7_out, in_1, in_16);
  xor xor_8 (xor_8_out, in_1, in_18);
  and and_1 (and_1_out, in_3, not_1_out);
  and and_2 (and_2_out, xor_1_out, not_1_out);
  and and_3 (and_3_out, in_1, not_1_out);
  and and_4 (and_4_out, in_5, not_1_out);
  and and_5 (and_5_out, xor_2_out, not_1_out);
  and and_6 (and_6_out, in_7, not_1_out);
  and and_7 (and_7_out, not_1_out, xor_3_out);
  and and_8 (and_8_out, in_9, not_1_out);
  and and_9 (and_9_out, not_1_out, xor_4_out);
  and and_10 (and_10_out, in_11, not_1_out);
  and and_11 (and_11_out, xor_5_out, not_1_out);
  and and_12 (and_12_out, in_13, not_1_out);
  and and_13 (and_13_out, xor_6_out, not_1_out);
  and and_14 (and_14_out, in_15, not_1_out);
  and and_15 (and_15_out, not_1_out, xor_7_out);
  and and_16 (and_16_out, not_1_out, in_17);
  and and_17 (and_17_out, not_1_out, xor_8_out);
  FA fa_1 (.Cin(and_1_out), .x(and_2_out), .y(and_3_out), .S(out_19), .Cout(fa_1_cout));
  FA fa_2 (.Cin(and_4_out), .x(and_5_out), .y(fa_1_cout), .S(out_20), .Cout(fa_2_cout));
  FA fa_3 (.Cin(and_6_out), .x(and_7_out), .y(fa_2_cout), .S(out_21), .Cout(fa_3_cout));
  FA fa_4 (.Cin(and_8_out), .x(and_9_out), .y(fa_3_cout), .S(out_22), .Cout(fa_4_cout));
  FA fa_5 (.Cin(and_10_out), .x(and_11_out), .y(fa_4_cout), .S(out_23), .Cout(fa_5_cout));
  FA fa_6 (.Cin(and_12_out), .x(and_13_out), .y(fa_5_cout), .S(out_24), .Cout(fa_6_cout));
  FA fa_7 (.Cin(and_14_out), .x(and_15_out), .y(fa_6_cout), .S(out_25), .Cout(fa_7_cout));
  FA fa_8 (.Cin(and_16_out), .x(and_17_out), .y(fa_7_cout), .S(out_26), .Cout(out_27));
endmodule

module _7SEGMENT (
  input  E,
  input  S3,
  input  S2,
  input  S1,
  input  S0,
  output a,
  output b,
  output c,
  output d,
  output e_2,
  output f,
  output g
);

  wire and_1_out, and_2_out, and_3_out, and_4_out, and_5_out, and_6_out, and_7_out, and_8_out, and_9_out,
       and_10_out, and_11_out, and_12_out, and_13_out, and_14_out, and_15_out, and_16_out, and_17_out,
       and_18_out, and_19_out, and_20_out, and_21_out, and_22_out, and_23_out, not_1_out, not_2_out,
       not_3_out, not_4_out, not_5_out, not_6_out, not_7_out, not_8_out, not_9_out, not_10_out, not_11_out,
       not_12_out, not_13_out, not_14_out, not_15_out, not_16_out, not_17_out, not_18_out, not_19_out,
       not_20_out, not_21_out, not_22_out, not_23_out, not_24_out, not_25_out, not_26_out, not_27_out,
       not_28_out, not_29_out, not_30_out, not_31_out, not_32_out, not_33_out, not_34_out, or_2_out, or_3_out;

  not not_1 (not_1_out, S2);
  not not_2 (not_2_out, S0);
  not not_3 (not_3_out, S3);
  not not_4 (not_4_out, S2);
  not not_5 (not_5_out, S3);
  not not_6 (not_6_out, S1);
  not not_7 (not_7_out, S0);
  not not_8 (not_8_out, S2);
  not not_9 (not_9_out, S1);
  not not_10 (not_10_out, S3);
  not not_11 (not_11_out, S2);
  not not_12 (not_12_out, S1);
  not not_13 (not_13_out, S3);
  not not_14 (not_14_out, S3);
  not not_15 (not_15_out, S2);
  not not_16 (not_16_out, S0);
  not not_17 (not_17_out, S2);
  not not_18 (not_18_out, S0);
  not not_19 (not_19_out, S1);
  not not_20 (not_20_out, S2);
  not not_21 (not_21_out, S0);
  not not_22 (not_22_out, S0);
  not not_23 (not_23_out, S1);
  not not_24 (not_24_out, S0);
  not not_25 (not_25_out, S1);
  not not_26 (not_26_out, S0);
  not not_27 (not_27_out, S2);
  not not_28 (not_28_out, S1);
  not not_29 (not_29_out, S0);
  not not_30 (not_30_out, E);
  and and_1 (and_1_out, not_1_out, not_2_out);
  and and_2 (and_2_out, S2, S0);
  and and_3 (and_3_out, not_3_out, not_4_out);
  and and_4 (and_4_out, not_5_out, not_6_out, not_7_out);
  and and_5 (and_5_out, not_8_out, not_9_out);
  and and_6 (and_6_out, not_10_out, S1, S0);
  and and_7 (and_7_out, not_11_out, not_12_out);
  and and_8 (and_8_out, not_13_out, S0);
  and and_9 (and_9_out, not_14_out, S2);
  not not_31 (not_31_out, E);
  and and_10 (and_10_out, not_15_out, not_16_out);
  and and_11 (and_11_out, not_17_out, S1);
  and and_12 (and_12_out, S1, not_18_out);
  and and_13 (and_13_out, S2, not_19_out, S0);
  not not_32 (not_32_out, E);
  and and_14 (and_14_out, not_20_out, not_21_out);
  and and_15 (and_15_out, S1, not_22_out);
  and and_16 (and_16_out, S3, S1);
  and and_17 (and_17_out, S3, S2);
  not not_33 (not_33_out, E);
  and and_18 (and_18_out, not_23_out, not_24_out);
  and and_19 (and_19_out, S2, not_25_out);
  and and_20 (and_20_out, S2, not_26_out);
  not not_34 (not_34_out, E);
  and and_21 (and_21_out, not_27_out, S1);
  and and_22 (and_22_out, S2, not_28_out);
  and and_23 (and_23_out, S2, not_29_out);
  or or_1 (a, not_30_out, and_1_out, S1, and_2_out, S3);
  or or_2 (or_2_out, and_3_out, and_4_out, and_5_out, and_6_out);
  and and_24 (c, E, or_3_out);
  or or_3 (or_3_out, and_7_out, and_8_out, and_9_out);
  or or_4 (d, not_31_out, and_10_out, and_11_out, and_12_out, and_13_out, S3);
  or or_5 (e_2, not_32_out, and_14_out, and_15_out, and_16_out, and_17_out);
  or or_6 (f, not_33_out, and_18_out, and_19_out, and_20_out, S3);
  or or_7 (g, not_34_out, and_21_out, and_22_out, and_23_out, S3);
  and and_25 (b, E, or_2_out);
endmodule

module _8bit7segment (
  input  in_1,
  input  in_2,
  input  in_3,
  input  in_4,
  input  in_5,
  input  in_6,
  input  in_7,
  input  in_8,
  output out_9,
  output out_10,
  output out_11,
  output out_12,
  output out_13,
  output out_14,
  output out_15,
  output out_16,
  output out_17,
  output out_18,
  output out_19,
  output out_20
);

  wire [7:0] divider_1_rem, divider_2_rem;
  wire [7:4] divider_1_out, divider_2_out, moduluscircuit_1_out_2;

  Divider divider_1 (
    .a({in_8, in_7, in_6, in_5, in_4, in_3, in_2, in_1}), .b(8'h64),
    .out({divider_1_out, out_12, out_11, out_10, out_9}), .rem(divider_1_rem));  // open: upper
  Divider divider_2 (
    .a(divider_1_rem), .b(8'ha), .out({divider_2_out, out_16, out_15, out_14, out_13}), .rem(divider_2_rem));  // open: upper
  moduluscircuit moduluscircuit_1 (
    .in_1(divider_2_rem), .out_2({moduluscircuit_1_out_2, out_20, out_19, out_18, out_17}));
endmodule

module moduluscircuit (
  input  [7:0] in_1,
  output [7:0] out_2
);

  wire [7:0] divider_1_out, multiplier_1_out;

  Divider divider_1 (.a(in_1), .b(8'ha), .out(divider_1_out));  // open: upper, rem
  Multiplier multiplier_1 (.a(divider_1_out), .b(8'ha), .out(multiplier_1_out));  // open: cin, cout
  Subtractor subtractor_1 (.a(in_1), .b(multiplier_1_out), .out(out_2));  // open: bin, bout
endmodule
