// Logisim project new counter.circ as structural Verilog: 6 circuits, main circuit JK NEW
module JK_NEW (
  input  J,
  input  K,
  input  CK,
  input  RS,
  output Q,
  output nQ
);

  wire and_1_out, and_2_out, or_1_out;

  and and_1 (and_1_out, J, nQ);
  and and_2 (and_2_out, ~K, Q);  // AND_Gate
  or or_1 (or_1_out, and_1_out, and_2_out);
  D_Flip_Flop d_ff_1 (.clk(CK), .D(or_1_out), .Q(Q), .Qn(nQ), .reset(RS));  // open: preset, en
endmodule

module draft (
  input  in_1,
  input  in_2,
  input  in_3,
  input  in_4,
  input  in_5,
  input  in_6,
  input  in_7,
  input  in_8
);

  // AND_Gate and_1 is placed but not wired
  // AND_Gate and_2 is placed but not wired
  JK_NEW jk_new_1 ();  // open: J, K, Q, nQ, CK, RS
  // OR_Gate or_1 is placed but not wired
  // AND_Gate and_3 is placed but not wired
  // AND_Gate and_4 is placed but not wired
  JK_NEW jk_new_2 ();  // open: J, K, Q, nQ, CK, RS
  // OR_Gate or_2 is placed but not wired
  // AND_Gate and_5 is placed but not wired
  // AND_Gate and_6 is placed but not wired
  JK_NEW jk_new_3 ();  // open: J, K, Q, nQ, CK, RS
  // OR_Gate or_3 is placed but not wired
  // AND_Gate and_7 is placed but not wired
  JK_NEW jk_new_4 ();  // open: J, K, Q, nQ, CK, RS
  // AND_Gate and_8 is placed but not wired
  // OR_Gate or_4 is placed but not wired
  // AND_Gate and_9 is placed but not wired
  // AND_Gate and_10 is placed but not wired
  JK_NEW jk_new_5 ();  // open: J, K, Q, nQ, CK, RS
  // OR_Gate or_5 is placed but not wired
  // AND_Gate and_11 is placed but not wired
  JK_NEW jk_new_6 ();  // open: J, K, Q, nQ, CK, RS
  // OR_Gate or_6 is placed but not wired
  // AND_Gate and_12 is placed but not wired
  // AND_Gate and_13 is placed but not wired
  JK_NEW jk_new_7 ();  // open: J, K, Q, nQ, CK, RS
  // OR_Gate or_7 is placed but not wired
  // AND_Gate and_14 is placed but not wired
  // AND_Gate and_15 is placed but not wired
  JK_NEW jk_new_8 ();  // open: J, K, Q, nQ, CK, RS
  // OR_Gate or_8 is placed but not wired
  // AND_Gate and_16 is placed but not wired
  // AND_Gate and_17 is placed but not wired
endmodule

module JK_old (
  input  J,
  input  K,
  output Q,
  output nQ
);

  wire C_out, nand_1_out, nand_2_out;

  Clock C (.out(C_out));
  nand nand_1 (nand_1_out, nQ, J, C_out);
  nand nand_2 (nand_2_out, C_out, K, Q);
  nand nand_3 (Q, nand_1_out, nQ);
  nand nand_4 (nQ, Q, nand_2_out);
endmodule

module JK_leader_follower_circuit (
  input  J,
  input  K,
  output Q,
  output nQ
);

  wire C_out, nand_1_out, nand_2_out, nand_3_out, nand_4_out, nand_5_out, nand_6_out, not_1_out;

  Clock C (.out(C_out));
  nand nand_1 (nand_1_out, nQ, J, C_out);
  nand nand_2 (nand_2_out, C_out, K, Q);
  nand nand_3 (nand_3_out, nand_1_out, nand_4_out);
  nand nand_4 (nand_4_out, nand_3_out, nand_2_out);
  not not_1 (not_1_out, C_out);
  nand nand_5 (nand_5_out, nand_3_out, not_1_out);
  nand nand_6 (nand_6_out, not_1_out, nand_4_out);
  nand nand_7 (Q, nand_5_out, nQ);
  nand nand_8 (nQ, Q, nand_6_out);
endmodule

module up_counter (
  input  CK,
  input  RS,
  output out_3,
  output out_4,
  output out_5,
  output out_6,
  output out_7,
  output out_8,
  output out_9,
  output out_10
);

  wire and_1_out, and_2_out, and_3_out, and_4_out, and_5_out, and_6_out, and_7_out, and_8_out, and_9_out,
       and_10_out, and_11_out, and_12_out, and_13_out, and_14_out, jk_new_1_nq, jk_new_2_nq, jk_new_3_nq,
       jk_new_4_nq, jk_new_5_nq, jk_new_6_nq, jk_new_7_nq, not_1_out, or_1_out, or_2_out, or_3_out, or_4_out,
       or_5_out, or_6_out, or_7_out;

  JK_NEW jk_new_1 (.J(1'b1), .K(1'b1), .Q(out_10), .nQ(jk_new_1_nq), .CK(CK), .RS(RS));
  not not_1 (not_1_out, 1'b1);
  and and_1 (and_1_out, 1'b1, out_10);
  and and_2 (and_2_out, jk_new_1_nq, not_1_out);
  JK_NEW jk_new_2 (.J(or_1_out), .K(or_1_out), .Q(out_9), .nQ(jk_new_2_nq), .CK(CK), .RS(RS));
  or or_1 (or_1_out, and_1_out, and_2_out);
  and and_3 (and_3_out, and_1_out, out_9);
  and and_4 (and_4_out, jk_new_2_nq, and_2_out);
  JK_NEW jk_new_3 (.J(or_2_out), .K(or_2_out), .Q(out_8), .nQ(jk_new_3_nq), .CK(CK), .RS(RS));
  or or_2 (or_2_out, and_3_out, and_4_out);
  and and_5 (and_5_out, and_3_out, out_8);
  and and_6 (and_6_out, jk_new_3_nq, and_4_out);
  JK_NEW jk_new_4 (.J(or_3_out), .K(or_3_out), .Q(out_7), .nQ(jk_new_4_nq), .CK(CK), .RS(RS));
  or or_3 (or_3_out, and_5_out, and_6_out);
  and and_7 (and_7_out, and_5_out, out_7);
  and and_8 (and_8_out, jk_new_4_nq, and_6_out);
  JK_NEW jk_new_5 (.J(or_4_out), .K(or_4_out), .Q(out_6), .nQ(jk_new_5_nq), .CK(CK), .RS(RS));
  or or_4 (or_4_out, and_7_out, and_8_out);
  and and_9 (and_9_out, and_7_out, out_6);
  and and_10 (and_10_out, jk_new_5_nq, and_8_out);
  JK_NEW jk_new_6 (.J(or_5_out), .K(or_5_out), .Q(out_5), .nQ(jk_new_6_nq), .CK(CK), .RS(RS));
  or or_5 (or_5_out, and_9_out, and_10_out);
  and and_11 (and_11_out, and_9_out, out_5);
  and and_12 (and_12_out, jk_new_6_nq, and_10_out);
  JK_NEW jk_new_7 (.J(or_6_out), .K(or_6_out), .Q(out_4), .nQ(jk_new_7_nq), .CK(CK), .RS(RS));
  or or_6 (or_6_out, and_11_out, and_12_out);
  and and_13 (and_13_out, and_11_out, out_4);
  and and_14 (and_14_out, jk_new_7_nq, and_12_out);
  JK_NEW jk_new_8 (.J(or_7_out), .K(or_7_out), .Q(out_3), .CK(CK), .RS(RS));  // open: nQ
  or or_7 (or_7_out, and_13_out, and_14_out);
endmodule

module down_counter (
  input  CK,
  input  RS,
  output out_3,
  output out_4,
  output out_5,
  output out_6,
  output out_7,
  output out_8,
  output out_9,
  output out_10
);

  wire and_1_out, and_2_out, and_3_out, and_4_out, and_5_out, and_6_out, and_7_out, and_8_out, and_9_out,
       and_10_out, and_11_out, and_12_out, and_13_out, and_14_out, jk_new_1_nq, jk_new_2_nq, jk_new_3_nq,
       jk_new_4_nq, jk_new_5_nq, jk_new_6_nq, jk_new_7_nq, not_1_out, or_1_out, or_2_out, or_3_out, or_4_out,
       or_5_out, or_6_out, or_7_out;

  JK_NEW jk_new_1 (.J(1'b1), .K(1'b1), .Q(out_10), .nQ(jk_new_1_nq), .CK(CK), .RS(RS));
  not not_1 (not_1_out, 1'b0);
  and and_1 (and_1_out, 1'b0, out_10);
  and and_2 (and_2_out, jk_new_1_nq, not_1_out);
  JK_NEW jk_new_2 (.J(or_1_out), .K(or_1_out), .Q(out_9), .nQ(jk_new_2_nq), .CK(CK), .RS(RS));
  or or_1 (or_1_out, and_1_out, and_2_out);
  and and_3 (and_3_out, and_1_out, out_9);
  and and_4 (and_4_out, jk_new_2_nq, and_2_out);
  JK_NEW jk_new_3 (.J(or_2_out), .K(or_2_out), .Q(out_8), .nQ(jk_new_3_nq), .CK(CK), .RS(RS));
  or or_2 (or_2_out, and_3_out, and_4_out);
  and and_5 (and_5_out, and_3_out, out_8);
  and and_6 (and_6_out, jk_new_3_nq, and_4_out);
  JK_NEW jk_new_4 (.J(or_3_out), .K(or_3_out), .Q(out_7), .nQ(jk_new_4_nq), .CK(CK), .RS(RS));
  or or_3 (or_3_out, and_5_out, and_6_out);
  and and_7 (and_7_out, and_5_out, out_7);
  and and_8 (and_8_out, jk_new_4_nq, and_6_out);
  JK_NEW jk_new_5 (.J(or_4_out), .K(or_4_out), .Q(out_6), .nQ(jk_new_5_nq), .CK(CK), .RS(RS));
  or or_4 (or_4_out, and_7_out, and_8_out);
  and and_9 (and_9_out, and_7_out, out_6);
  and and_10 (and_10_out, jk_new_5_nq, and_8_out);
  JK_NEW jk_new_6 (.J(or_5_out), .K(or_5_out), .Q(out_5), .nQ(jk_new_6_nq), .CK(CK), .RS(RS));
  or or_5 (or_5_out, and_9_out, and_10_out);
  and and_11 (and_11_out, and_9_out, out_5);
  and and_12 (and_12_out, jk_new_6_nq, and_10_out);
  JK_NEW jk_new_7 (.J(or_6_out), .K(or_6_out), .Q(out_4), .nQ(jk_new_7_nq), .CK(CK), .RS(RS));
  or or_6 (or_6_out, and_11_out, and_12_out);
  and and_13 (and_13_out, and_11_out, out_4);
  and and_14 (and_14_out, jk_new_7_nq, and_12_out);
  JK_NEW jk_new_8 (.J(or_7_out), .K(or_7_out), .Q(out_3), .CK(CK), .RS(RS));  // open: nQ
  or or_7 (or_7_out, and_13_out, and_14_out);
endmodule
